# Fritzing sketch knock (saved by Fritzing 0.9.3b)
breadboards: 1

parts:
  Part1 = Arduino Uno (Rev3) - ICSP
  IR1 = TSOP312.., 314.. [package=THT]
  J1 = Basic Servo
  S1 = Pushbutton [package="[THT]"]
  J2 = Piezo Speaker

nets:
  N1: Part1.D2, IR1.GND
  N2: Part1.D3_PWM, J2.pin2
  N3: Part1.D4, J1.pulse
  N4: Part1.D5_PWM, S1.Pin_3, S1.Pin_4
  5V: Part1.5V, IR1.Data, J1.vcc
  GND: Part1.GND, IR1.Vs, J1.gnd, S1.Pin_1, S1.Pin_2, J2.pin1

custom parts:
  Piezo Speaker: Piezo
